# Fritzing sketch bme280 (saved by Fritzing 0.9.4)
breadboards: 1

parts:
  Arduino_Nano = Arduino Nano (Rev3.0)
  bme_280 = BME280 Breakout

nets:
  GND: Arduino_Nano.GND, bme_280.GND
  N1: Arduino_Nano.A5, bme_280.SDI/SDA
  N2: Arduino_Nano.A4, bme_280.SCK/SCL
  3V3: Arduino_Nano.3V3, bme_280.3.3V

// code stored in the sketch: bme280_ex.ino
#include <Adafruit_BME280.h>

Adafruit_BME280 bme; //SENSORE PRESSIONE,UMIDITA', TEMPERATURA

void setup() {
     
  //Initialize serial and wait for port to open:
  Serial.begin(9600);
  while (!Serial) {
    ; // wait for serial port to connect. Needed for native USB port only
  }


//SENSORI METEO
   Serial.begin(9600);
   if (!bme.begin(0x76)) {
    Serial.println("Non ho trovato il sensore BME280!");
    while (1);
  }

    Serial.begin(9600);
    Serial.println("CCS811 test");
    if(!ccs.begin())
    {
      Serial.println("Failed to start sensor CSS811! Please check your wiring.");
      while(1);
    }

}


void loop() { 

float H = bme.readPressure() / 100.0F; //LEGGO LA PRESSIONE E LA DIVIDO PER 100F CHE SIGNIFICA IN HPA
float U = bme.readHumidity(); //LEGGO UMIDITA
float T = bme.readTemperature(); //LEGGO TEMPERATURA

Serial.println("SENSORI METEO");
Serial.println("Pressione: " + (String)H);
Serial.println("Umidità:" + (String)U);
Serial.println("Temperatura:" + (String)T);

}
